// Digital circuit Decoder2.dig as structural Verilog
module Decoder2 (
  input  [1:0] sel,
  output out_0,
  output out_1,
  output out_2,
  output out_3
);

  and and_1 (out_0, ~sel[0], ~sel[1]);  // And
  and and_2 (out_1, sel[0], ~sel[1]);  // And
  and and_3 (out_2, ~sel[0], sel[1]);  // And
  and and_4 (out_3, sel[0], sel[1]);
endmodule
