// Digital circuit Demux1.dig as structural Verilog
module Demux1 (
  input  sel,
  input  in,
  output out_0,
  output out_1
);

  and and_1 (out_0, in, ~sel);  // And
  and and_2 (out_1, in, sel);
endmodule
