// Digital circuit DriverInv.dig as structural Verilog
module DriverInv (
  input  in,
  input  sel,
  output out
);

  wire T1_d, T3_d, T6_s, T7_d;

  PFET T1 (.G(sel), .S(1'b1), .D(T1_d));
  NFET T2 (.G(sel), .D(T1_d), .S(1'b0));
  PFET T7 (.G(in), .S(1'b1), .D(T7_d));
  NFET T8 (.G(in), .D(T7_d), .S(1'b0));
  PFET T3 (.G(sel), .S(1'b1), .D(T3_d));
  PFET T5 (.G(T7_d), .S(T3_d), .D(out));
  NFET T6 (.G(T7_d), .D(out), .S(T6_s));
  NFET T4 (.G(T1_d), .D(T6_s), .S(1'b0));
endmodule
