// Digital circuit JK-ff.dig as structural Verilog
// Clock edges triggert JK flip-flop. 
// A rising edge at the clock input is converted into a pulse 
// whose duration is just sufficient to switch the flip-flop.
// {{de Taktflanken gesteuerters JK-Flipflop. Eine steigende
// Flanke am Takteingang wird in einem Impuls 
// umgeformt, der gerade ausreicht, um das Flipflop
// umzuschalten.}}
module JK_ff (
  input  J,
  input  C,
  input  K,
  output Q,
  output nQ
);

  wire and_1_out, and_2_out, and_3_out, not_1_out, not_2_out, not_3_out;

  not not_1 (not_1_out, C);
  not not_2 (not_2_out, not_1_out);
  not not_3 (not_3_out, not_2_out);
  and and_1 (and_1_out, not_3_out, C);
  and and_2 (and_2_out, Q, K, and_1_out);
  and and_3 (and_3_out, and_1_out, J, nQ);
  nor nor_1 (Q, and_2_out, nQ);
  nor nor_2 (nQ, Q, and_3_out);

  // Notes on the sheet:
  //   J: Input to set the flip-flop
  //   {{de Eingang zum Setzen des Flipflops.}}
  //   Q: The bit stored in the flip-flop.
  //   {{de Das im Flipflop gespeicherte Bit.}}
  //   nQ: The inverted stored bit.
  //   {{de Das inverse gespeicherte Bit.}}
  //   K: Input to clear the flip-flop.
  //   {{de Eingang zum Löschen des Flipflops.}}
endmodule
