// Digital circuit Mux1.dig as structural Verilog
module Mux1 (
  input  in_0,
  input  in_1,
  input  sel,
  output out
);

  wire and_1_out, and_2_out;

  and and_1 (and_1_out, in_0, ~sel);  // And
  and and_2 (and_2_out, in_1, sel);
  or or_1 (out, and_1_out, and_2_out);
endmodule
