// Digital circuit Mux2.dig as structural Verilog
module Mux2 (
  input  [1:0] sel,
  input  in_0,
  input  in_1,
  input  in_2,
  input  in_3,
  output out
);

  wire and_1_out, and_2_out, and_3_out, and_4_out;

  and and_1 (and_1_out, in_0, ~sel[0], ~sel[1]);  // And
  and and_2 (and_2_out, in_1, sel[0], ~sel[1]);  // And
  and and_3 (and_3_out, in_2, ~sel[0], sel[1]);  // And
  and and_4 (and_4_out, in_3, sel[0], sel[1]);
  or or_1 (out, and_1_out, and_2_out, and_3_out, and_4_out);
endmodule
