// Digital circuit NAnd3.dig as structural Verilog
module NAnd3 (
  input  In_1,
  input  In_3,
  input  In_2,
  output Y
);

  wire T4_s, T5_s;

  PFET T1 (.G(In_1), .S(1'b1), .D(Y));
  NFET T4 (.G(In_1), .D(Y), .S(T4_s));
  NFET T5 (.G(In_2), .D(T4_s), .S(T5_s));
  NFET T6 (.G(In_3), .D(T5_s), .S(1'b0));
  PFET T2 (.G(In_2), .S(1'b1), .D(Y));
  PFET T3 (.G(In_3), .S(1'b1), .D(Y));
endmodule
