// Digital circuit Or3.dig as structural Verilog
module Or3 (
  input  In_1,
  input  In_3,
  input  In_2,
  output Y
);

  wire T1_d, T2_d, T3_d;

  PFET T1 (.G(In_1), .S(1'b1), .D(T1_d));
  PFET T2 (.G(In_2), .S(T1_d), .D(T2_d));
  PFET T3 (.G(In_3), .S(T2_d), .D(T3_d));
  NFET T4 (.G(In_1), .D(T3_d), .S(1'b0));
  NFET T5 (.G(In_2), .D(T3_d), .S(1'b0));
  NFET T6 (.G(In_3), .D(T3_d), .S(1'b0));
  PFET T7 (.G(T3_d), .S(1'b1), .D(Y));
  NFET T8 (.G(T3_d), .D(Y), .S(1'b0));
endmodule
