// Digital circuit T-ff-en.dig as structural Verilog
module T_ff_en (
  input  C,
  input  T,
  output Q,
  output nQ
);

  wire and_1_out, and_2_out, and_3_out, not_1_out, not_2_out, not_3_out;

  not not_1 (not_1_out, C);
  not not_2 (not_2_out, not_1_out);
  not not_3 (not_3_out, not_2_out);
  and and_1 (and_1_out, T, C, not_3_out);
  and and_2 (and_2_out, Q, and_1_out);
  and and_3 (and_3_out, and_1_out, nQ);
  nor nor_1 (Q, and_2_out, nQ);
  nor nor_2 (nQ, Q, and_3_out);
endmodule
