// Digital circuit T-ff.dig as structural Verilog
module T_ff (
  input  C,
  output Q,
  output nQ
);

  wire and_1_out, and_2_out, and_3_out, delay_1_out, not_1_out;

  not not_1 (not_1_out, C);
  Delay delay_1 (.in(not_1_out), .out(delay_1_out));
  and and_1 (and_1_out, delay_1_out, C);
  and and_2 (and_2_out, Q, and_1_out);
  and and_3 (and_3_out, and_1_out, nQ);
  nor nor_1 (Q, and_2_out, nQ);
  nor nor_2 (nQ, Q, and_3_out);
endmodule
