// Digital circuit ins1.dig as structural Verilog
module ins1 (
  input  in_1,
  input  in_2,
  output Y
);

  wire T3_s;

  PFET T1 (.G(in_1), .S(1'b1), .D(Y));
  NFET T3 (.G(in_1), .D(Y), .S(T3_s));
  NFET T4 (.G(in_2), .D(T3_s), .S(1'b0));
  PFET T2 (.G(in_2), .S(1'b1), .D(Y));
endmodule
