// Digital circuit ins3.dig as structural Verilog
module ins3 (
  input  in_1,
  input  in_2,
  output Y
);

  wire T1_d, T5_s;

  PFET T1 (.G(in_2), .S(1'b1), .D(T1_d));
  NFET T2 (.G(in_2), .D(T1_d), .S(1'b0));
  PFET T3 (.G(in_1), .S(1'b1), .D(Y));
  NFET T5 (.G(in_1), .D(Y), .S(T5_s));
  NFET T6 (.G(T1_d), .D(T5_s), .S(1'b0));
  PFET T4 (.G(T1_d), .S(1'b1), .D(Y));
endmodule
