// Digital circuit ins4.dig as structural Verilog
module ins4 (
  input  in_1,
  input  in_2,
  output Y
);

  wire T1_d, T2_d;

  PFET T1 (.G(in_1), .S(1'b1), .D(T1_d));
  PFET T2 (.G(in_2), .S(T1_d), .D(T2_d));
  NFET T4 (.G(in_2), .D(T2_d), .S(1'b0));
  NFET T3 (.G(in_1), .D(T2_d), .S(1'b0));
  PFET T5 (.G(T2_d), .S(1'b1), .D(Y));
  NFET T6 (.G(T2_d), .D(Y), .S(1'b0));
endmodule
