// Digital circuit ins6.dig as structural Verilog
module ins6 (
  input  in_1,
  input  in_2,
  output Y
);

  wire T1_d, T3_d;

  PFET T3 (.G(in_2), .S(1'b1), .D(T3_d));
  NFET T2 (.G(in_2), .D(T3_d), .S(1'b0));
  PFET T1 (.G(in_1), .S(1'b1), .D(T1_d));
  PFET T2_2 (.G(T3_d), .S(T1_d), .D(Y));
  NFET T4 (.G(T3_d), .D(Y), .S(1'b0));
  NFET T3_2 (.G(in_1), .D(Y), .S(1'b0));
endmodule
