// Digital circuit ins1.dig as structural Verilog
module ins1 (
  input  In_1,
  input  In_2,
  output Y
);

  wire T3_s;

  PFET T1 (.G(In_1), .S(1'b1), .D(Y));
  NFET T3 (.G(In_1), .D(Y), .S(T3_s));
  NFET T4 (.G(In_2), .D(T3_s), .S(1'b0));
  PFET T2 (.G(In_2), .S(1'b1), .D(Y));
endmodule
