// Digital circuit ins10.dig as structural Verilog
module ins10 (
  input  In_1,
  input  In_2,
  output Y
);

  wire T1_d, T5_s;

  PFET T1 (.G(In_1), .S(1'b1), .D(T1_d));
  NFET T2 (.G(In_1), .D(T1_d), .S(1'b0));
  PFET T3 (.G(T1_d), .S(1'b1), .D(Y));
  NFET T5 (.G(T1_d), .D(Y), .S(T5_s));
  NFET T6 (.G(In_2), .D(T5_s), .S(1'b0));
  PFET T4 (.G(In_2), .S(1'b1), .D(Y));
endmodule
