// Digital circuit ins2.dig as structural Verilog
module ins2 (
  input  In_1,
  input  In_2,
  output Y
);

  wire T1_d, T3_s;

  PFET T1 (.G(In_1), .S(1'b1), .D(T1_d));
  NFET T3 (.G(In_1), .D(T1_d), .S(T3_s));
  NFET T4 (.G(In_2), .D(T3_s), .S(1'b0));
  PFET T2 (.G(In_2), .S(1'b1), .D(T1_d));
  PFET T5 (.G(T1_d), .S(1'b1), .D(Y));
  NFET T6 (.G(T1_d), .D(Y), .S(1'b0));
endmodule
