// Digital circuit ins7.dig as structural Verilog
// Gate Diffusion Input (GDI) xor
// {{de Gate Diffusion Input (GDI) xor}}
module ins7 (
  input  in_1,
  input  in_2,
  output Y
);

  wire pfet_1_d;

  PFET pfet_1 (.G(in_2), .S(1'b1), .D(pfet_1_d));
  NFET nfet_1 (.G(in_2), .D(pfet_1_d), .S(1'b0));
  PFET #(.unidirectional("true")) pfet_2 (.G(in_1), .S(in_2), .D(Y));
  NFET #(.unidirectional("true")) nfet_2 (.G(in_1), .D(Y), .S(pfet_1_d));
endmodule
