// Digital circuit ins9.dig as structural Verilog
module ins9 (
  input  In_1,
  input  In_2,
  output Y
);

  wire T1_d, T3_d;

  PFET T1 (.G(In_1), .S(1'b1), .D(T1_d));
  NFET T2 (.G(In_1), .D(T1_d), .S(1'b0));
  PFET T3 (.G(T1_d), .S(1'b1), .D(T3_d));
  PFET T4 (.G(In_2), .S(T3_d), .D(Y));
  NFET T6 (.G(In_2), .D(Y), .S(1'b0));
  NFET T5 (.G(T1_d), .D(Y), .S(1'b0));
endmodule
